# Fritzing sketch Sơ đồ nối Xe Adruino (saved by Fritzing 0.9.9b)

parts:
  ESP32_-_Back1 = ESP32 - CAM
  L298N1 = L298N DC motor driver
  M1 = gear-motor
  M2 = gear-motor
  M3 = gear-motor
  M4 = gear-motor
  U1 = LIPO-2000mAh [package=lipo-2000]
  HC-SR04_Sensor_1 = HC-SR04 Ultrasonic Distance Sensor
  e-radionica_com1 = LM393 LDR breakout [part_number=100027]
  Enc1 = shaft encoder
  HC-SR04_Sensor_2 = HC-SR04 Ultrasonic Distance Sensor
  LED3 = LEDs [package=led10mm]
  LED4 = LEDs [package=led10mm]
  LED5 = LEDs [package=led10mm]
  LED6 = LEDs [package=led10mm]
  Part1 = Adafruit INA219 [part_number="Adafruit #904"]
  U5 = ESP32-38PinWide [part_number=ESP32-38PinWide]
  J2 = Piezo Speaker

nets:
  N1: ESP32_-_Back1.3.3V, ESP32_-_Back1.GPIO16, U5.3.3
  N2: ESP32_-_Back1.GPIO3_/_RX, U5.GPIO16
  N3: ESP32_-_Back1.GPIO1_/_TX, U5.GPIO17
  GND: ESP32_-_Back1.GND, U5.GND
  N4: L298N1.12V, U1.+
  N5: L298N1.GND, U1.-
  5V: L298N1.5V, U5.VIN
  N6: L298N1.ENA, U5.GPIO23
  N7: L298N1.ENB, U5.GPIO5
  N8: L298N1.IN1, U5.GPIO22
  N9: L298N1.IN2, U5.GPIO21
  N10: L298N1.IN3, U5.GPIO19
  N11: L298N1.IN4, U5.GPIO18
  N12: M1.pin_1, M4.pin_1
  N13: M1.pin_2, M4.pin_2
  N14: M2.pin_1, M3.pin_1
  N15: M2.pin_2, M3.pin_2
  N16: HC-SR04_Sensor_1.TRIG, U5.GPIO14
  N17: HC-SR04_Sensor_1.ECHO, U5.GPIO27
  N18: e-radionica_com1.AO, U5.GPIO36
  N19: e-radionica_com1.DO, U5.GPIO39
  N20: Enc1.OUT, U5.GPIO13
  N21: HC-SR04_Sensor_2.TRIG, U5.GPIO12
  N22: HC-SR04_Sensor_2.ECHO, U5.GPIO35
  N23: LED3.A, U5.GPIO25
  N24: LED4.A, U5.GPIO33
  N25: LED5.A, U5.GPIO26
  N26: LED6.A, U5.GPIO32
  N27: Part1.SCL, U5.GPIO1
  N28: Part1.SDA, U5.GPIO3
  N29: U5.GPIO4, J2.pin2

custom parts:
  ESP32 - CAM: The ESP32-CAM has a very competitive small-size camera module that can operate independently as a minimum system with a footprint of only 27*40.5*4.5mm and a deep sleep current of up to 6mA.
  L298N DC motor driver: 2x DC motor driver with 78M05 positive voltage regulator (7..35 V) L298N: max 46 V, 2 A Set 5 V Enable jumper to enable 5 V regultor (needed for the L298N) and +5 V output at screw terminal or supply external +5 V at screw terminal Set ENA and/or ENB to +5 V to enable motor permanently or supply ENA and/or ENB with PWM signal IN1 and IN2 set rotation directory for motor A (OUT1/OUT2) IN2 and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
  Adafruit INA219: This breakout board will solve all your power-monitoring problems. Instead of struggling with two multimeters, you can just use the handy INA219B chip on this breakout to both measure both the high side voltage and DC current draw over I2C with 1% precision. Most current-measuring devices such as our current panel meter are only good for low side measuring. That means that unless you want to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
  ESP32-38PinWide: Generic 38-Pin ESP32 with wide format (only access to one side of pins on a breadboard) based on Stephen Lilley's HiLetgo ESP-WROOM-32 ESP32 ESP-32S Development Board.
